# Fritzing sketch Protisruti_hardware (saved by Fritzing 0.9.3b)
circuit board: 8.46667cm x 5.64444cm
breadboards: 1

parts:
  Raspberry_Pi_1 = Raspberry Pi 3 [part_number=RPI-3-V1.2]
  VCC1 = Battery
  R1 = Resistor [tolerance=±5% resistance=220 package=THT]
  R2 = Photocell (LDR) [package=THT]
  U1 = Voltage Regulator [package=to220-adj]
  DS1 = DS18B20 1-Wire Temperature Sensor [part_number=DS18B20]
  R3 = Resistor [tolerance=±5% resistance=220 package=THT]
  C1 = Capacitor Polarized [package=cpol-radial-100uf-25v]
  Part1 = Soil Moisture Sensor
  U2 = 2-Channel 5v Relay Shield [package=relay-2ch5v10a]
  WATER_PUMP1 = water pump/motor  # not connected
  D1 = LTE-302 [package=lte-302]

nets:
  N1: Raspberry_Pi_1.GPIO17, R2.pin_1, C1.-
  N2: Raspberry_Pi_1.GPIO27, U2.IN2
  N3: Raspberry_Pi_1.GPIO6, U2.IN1
  N4: Raspberry_Pi_1.GPIO21, Part1.SIG
  VCC: Raspberry_Pi_1.5V, R2.pin_0, DS1.VDD, R3.Pin_0, Part1.VCC, U2.VCC
  N5: VCC1.-, R1.Pin_1, U1.IN
  N6: VCC1.+, U1.ADJ
  N7: R1.Pin_0, D1.C
  N8: U1.OUT, U2.K2-In
  GND: DS1.GND, C1.+, Part1.GND, U2.GND
  N9: DS1.DQ, R3.Pin_1

custom parts:
  2-Channel 5v Relay Shield: 2 Channel 5v Relay Shield w. 2x SPD-06VDC-SD-C
  water pump/motor: WATER PUMP BY ARDUBLOCKTR
